// Digital circuit q_4.dig as structural Verilog
module q_4 (
  input  x,
  input  y,
  input  z,
  output F_x_y_z
);

  wire and_1_out, and_2_out, not_1_out;

  not not_1 (not_1_out, y);
  and and_1 (and_1_out, x, y);
  and and_2 (and_2_out, not_1_out, z);
  or or_1 (F_x_y_z, and_1_out, not_1_out, and_2_out);
endmodule
