// Digital circuit q_8_3.dig as structural Verilog
module q_8_3 (
  input  I2,
  input  I1,
  output Z1,
  output Z0
);

  wire and_1_out, and_2_out, not_1_out, not_2_out;

  not not_1 (not_1_out, I2);
  not not_2 (not_2_out, I1);
  and and_1 (and_1_out, I2, not_2_out);
  and and_2 (and_2_out, I2, I1);
  or or_1 (Z1, and_1_out, and_2_out);
  and and_3 (Z0, not_1_out, I1);

  // Notes on the sheet:
  //   Gasser Ahmed - 06/11/2020
endmodule
