// Digital circuit Ahmed_Gasser_P1.dig as structural Verilog
module Ahmed_Gasser_P1 (
  input  X1,
  input  X2,
  input  X3,
  input  X0,
  input  in_5
);

  wire and_1_out, and_2_out, and_3_out, and_4_out, and_5_out, and_6_out, and_7_out, and_8_out, and_9_out,
       not_1_out, not_2_out, not_3_out, not_4_out;
  wire [3:0] xor_1_out;

  not not_1 (not_1_out, X3);
  not not_2 (not_2_out, X2);
  not not_3 (not_3_out, X1);
  not not_4 (not_4_out, X0);
  and and_1 (and_1_out, not_3_out, X0);
  and and_2 (and_2_out, not_2_out, X1, not_4_out);
  and and_3 (and_3_out, not_1_out, X2, X0);
  and and_4 (and_4_out, X3, X2, not_3_out);
  and and_5 (and_5_out, X1, X3);
  and and_6 (and_6_out, X1, not_2_out);
  and and_7 (and_7_out, X0, not_2_out);
  and and_8 (and_8_out, X0, not_2_out);
  and and_9 (and_9_out, X2, not_1_out);
  xor xor_1 (xor_1_out[0], X0, X1, X2, X3);
  or or_1 (xor_1_out[1], and_1_out, and_2_out, and_3_out, and_4_out);
  or or_2 (xor_1_out[2], and_5_out, and_6_out, and_7_out);
  or or_3 (xor_1_out[3], and_8_out, and_9_out);
  Seven_Seg_Hex seven_seg_hex_1 (.d(xor_1_out), .dp(in_5));

  // Notes on the sheet:
  //   Basic Circuit Layout for ECE 5484 Project 1
  //   Created by Gasser Ahmed, 06-24-2020
  //   Y1
  //   Y2
  //   Y3
  //   Y0
endmodule
