// Digital circuit P1_Starter_Circuit.dig as structural Verilog
module P1_Starter_Circuit (
  input  X1,
  input  X2,
  input  X3,
  input  X0,
  input  Y1,
  input  Y2,
  input  Y3,
  input  in_8
);

  wire not_1_out, not_2_out, not_3_out, not_4_out;
  wire [0:0] xor_1_out;

  not not_1 (not_1_out, X3);
  not not_2 (not_2_out, X2);
  not not_3 (not_3_out, X1);
  not not_4 (not_4_out, X0);
  xor xor_1 (xor_1_out[0], X0, X1, X2, X3);
  Seven_Seg_Hex seven_seg_hex_1 (.d({Y3, Y2, Y1, xor_1_out[0]}), .dp(in_8));

  // Notes on the sheet:
  //   Basic Circuit Layout for ECE 5484 Project 1
  //   Created by David McPherson, Virginia Tech
  //   Inputs for Y1, Y2, and Y3 are temporary. They are to be replaced by combinational
  //   logic circuits to produce Y1, Y2, and Y3 from inputs X0, X1, X2, and X3.
  //   Y0
endmodule
